# Fritzing sketch rangkaian (saved by Fritzing 0.9.2b)
breadboards: 1

parts:
  M1 = fc-51 [package=THT]
  M2 = fc-51 [package=THT]
  M3 = fc-51 [package=THT]
  M4 = fc-51 [package=THT]
  M5 = fc-51 [package=THT]
  M6 = fc-51 [package=THT]
  Part1 = Arduino Mega ADK (Rev3)
  M7 = fc-51 [package=THT]
  M8 = fc-51 [package=THT]
  M9 = fc-51 [package=THT]
  M10 = fc-51 [package=THT]
  M11 = fc-51 [package=THT]
  M12 = fc-51 [package=THT]
  M13 = fc-51 [package=THT]
  M14 = fc-51 [package=THT]
  M15 = fc-51 [package=THT]
  M16 = fc-51 [package=THT]
  M17 = fc-51 [package=THT]
  DFPlayer_Mini1 = DFPlayer MINI [package="DIP (Dual Inline) [THT]"]
  R1 = Resistor [tolerance=±10% resistance=1k package="0402 [SMD]"]
  Part2 = Adafruit STEMMA Speaker [part_number="Adafruit #3885"]

nets:
  N1: M1.pin1, Part1.D36
  GND: M1.pin2, M2.pin2, M3.pin2, M4.pin2, M5.pin2, M6.pin2, Part1.GND, M7.pin2, M8.pin2, M9.pin2, M10.pin2, M11.pin2, M12.pin2, M13.pin2, M14.pin2, M15.pin2, M16.pin2, M17.pin2, DFPlayer_Mini1.GND
  5V: M1.pin3, M2.pin3, M3.pin3, M4.pin3, M5.pin3, M6.pin3, Part1.5V, M7.pin3, M8.pin3, M9.pin3, M10.pin3, M11.pin3, M12.pin3, M13.pin3, M14.pin3, M15.pin3, M16.pin3, M17.pin3, DFPlayer_Mini1.VCC
  N2: M2.pin1, Part1.D34
  N3: M3.pin1, Part1.D32
  N4: M4.pin1, Part1.D30
  N5: M5.pin1, Part1.D28
  N6: M6.pin1, Part1.D26
  N7: Part1.D8_PWM, M17.pin1
  N8: Part1.D2_PWM, DFPlayer_Mini1.TX
  N9: Part1.D3_PWM, R1.Pin_0
  N10: Part1.D22, M8.pin1
  N11: Part1.D24, M7.pin1
  N12: Part1.D31, M9.pin1
  N13: Part1.D33, M10.pin1
  N14: Part1.D35, M11.pin1
  N15: Part1.D41, M12.pin1
  N16: Part1.D43, M13.pin1
  N17: Part1.D45, M14.pin1
  N18: Part1.D47, M15.pin1
  N19: Part1.D49, M16.pin1
  N20: DFPlayer_Mini1.RX, R1.Pin_1
  N21: DFPlayer_Mini1.SPK1, Part2.GND
  N22: DFPlayer_Mini1.SPK2, Part2.SIG

notes:
  Sensors
  0
  Sensors
  30
  Sensors
  45
  Sensors
  60
  Sensors
  90
  Sensors
  120
  Sensors
  135
  Sensors
  150
  Sensors
  180
  Sensors
  210
  Sensors
  225
  Sensors
  240
  Sensors
  270
  Sensors
  300
  Sensors
  315
  Sensors
  330
  Sensors
  360

custom parts:
  DFPlayer MINI: MP3 module by DFRobot.com for playing Music from an SD-Card. Supports WAV and MP3 files.
  Adafruit STEMMA Speaker: Hey, have you heard the good news? With Adafruit STEMMA boards you can easily and safely plug sensors and devices together, like this Adafruit STEMMA Speaker - Plug and Play Audio Amplifier. Like the name implies, it's got a class D audio amplifier on board, and our favorite little 1 Watt 8 ohm speaker. Connecting it up is easy - you only need ground, 3 to 5V power, and audio signal. The audio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
